# Fritzing sketch schematic (saved by Fritzing 0.9.3b)
breadboards: 1

parts:
  Part2 = MQ-4
  VCC2 = Battery block 9V
  IC2 = Voltage Regulator [package=to220-igo]
  U2 = ESP8266 NodeMCU LoLin module
  HC-SR04_Sensor_1 = HC-SR04 Ultrasonic Distance Sensor

nets:
  VCC: Part2.VCC, U2.3V3
  GND: Part2.GND, VCC2.-, IC2.GND, U2.GND, HC-SR04_Sensor_1.GND
  N1: Part2.AO, U2.A0
  N2: VCC2.+, IC2.IN, U2.Vin
  N3: IC2.OUT, HC-SR04_Sensor_1.VCC
  N4: U2.D1, HC-SR04_Sensor_1.TRIG
  N5: U2.D2, HC-SR04_Sensor_1.ECHO

custom parts:
  ESP8266 NodeMCU LoLin module: ESP8266 based NodeMCU
  HC-SR04 Ultrasonic Distance Sensor: The HC-SR04 is an ultrasonic distance sensor. It is capable of providing measurement for ranges of 2cm to 400cm. The module operates at 5V.
